// Logisim project SimpleALU.circ as structural Verilog: 4 circuits, main circuit Main
module _8BitALU (
  input  sub,
  input  \and ,
  input  \or ,
  input  \xor ,
  input  left_shift,
  input  right_shift,
  input  sub_flag,
  input  [7:0] rhs,
  input  [7:0] lhs,
  output [7:0] \output ,
  output carry_out
);

  wire [7:0] adder_1_out, and_1_out, bit_extender_1_out, or_1_out, shiftleft_1_out_2, shiftright_1_out_2,
       xor_1_out, xor_2_out;

  assign bit_extender_1_out = {{7{sub_flag}}, sub_flag};  // Bit_Extender bit_extender_1
  assign xor_1_out = bit_extender_1_out ^ rhs;  // XOR_Gate xor_1, 8 bits wide
  Adder adder_1 (.a(xor_1_out), .b(lhs), .out(adder_1_out), .cin(sub_flag), .cout(carry_out));
  assign and_1_out = rhs & lhs;  // AND_Gate and_1, 8 bits wide
  assign or_1_out = rhs | lhs;  // OR_Gate or_1, 8 bits wide
  assign xor_2_out = rhs ^ lhs;  // XOR_Gate xor_2, 8 bits wide
  ShiftLeft shiftleft_1 (.in_1(lhs), .out_2(shiftleft_1_out_2));
  ShiftRight shiftright_1 (.in_1(lhs), .out_2(shiftright_1_out_2));
  assign \output  = sub ? adder_1_out : 8'bz;  // Controlled_Buffer controlled_buffer_1
  assign \output  = \and  ? and_1_out : 8'bz;  // Controlled_Buffer controlled_buffer_2
  assign \output  = \or  ? or_1_out : 8'bz;  // Controlled_Buffer controlled_buffer_3
  assign \output  = \xor  ? xor_2_out : 8'bz;  // Controlled_Buffer controlled_buffer_4
  assign \output  = left_shift ? shiftleft_1_out_2 : 8'bz;  // Controlled_Buffer controlled_buffer_5
  assign \output  = right_shift ? shiftright_1_out_2 : 8'bz;  // Controlled_Buffer controlled_buffer_6
endmodule

module ShiftLeft (
  input  [7:0] in_1,
  output [7:0] out_2
);


  assign out_2 = {in_1[6:0], 1'b0};
endmodule

module ShiftRight (
  input  [7:0] in_1,
  output [7:0] out_2
);


  assign out_2 = {1'b0, in_1[7:1]};
endmodule

module Main (
  input  in_1,
  input  in_2,
  input  in_3,
  input  in_4,
  input  in_5,
  input  in_6,
  input  [7:0] in_7,
  input  [7:0] in_8,
  input  in_9,
  output [7:0] out_10,
  output out_11
);

  _8BitALU u_8bitalu_1 (
    .sub(in_1), .\and (in_2), .\or (in_3), .\xor (in_4), .left_shift(in_5), .right_shift(in_6),
    .sub_flag(in_9), .rhs(in_8), .lhs(in_7), .\output (out_10), .carry_out(out_11));
endmodule
